# Fritzing sketch Komputer Terapan (saved by Fritzing 0.9.3b)
breadboards: 1

parts:
  Part1 = Arduino Uno (Rev3)
  T1 = LM35 Temperature Sensor [package="TO92 [THT]"]
  LED1 = LED - 3mm [color="Red (633nm)" package="3 mm [THT]"]
  R1 = Resistor [tolerance=±5% resistance=220 package=THT]

nets:
  N1: Part1.A2, T1.Vout
  N2: Part1.D5_PWM, LED1.anode
  N3: Part1.5V, T1.+Vs
  GND: Part1.GND, T1.GND, R1.Pin_1
  N4: LED1.cathode, R1.Pin_0
